# Fritzing sketch Conexion (saved by Fritzing 0.9.3b)
breadboards: 1

parts:
  Componente1 = Arduino Nano (Rev3.0)
  Componente2 = RFID-RC522-v3

nets:
  GND: Componente1.GND, Componente2.GND
  N1: Componente1.D9, Componente2.RST
  N2: Componente1.D10, Componente2.SDA
  N3: Componente1.D11/MOSI, Componente2.MOSI
  N4: Componente1.D12/MISO, Componente2.MISO
  3V3: Componente1.3V3, Componente2.3.3V
  N5: Componente1.D13/SCK, Componente2.SCK

custom parts:
  RFID-RC522-v3: A simple China made RFID-RC522 Reader (6x4 cm); do check the pin labels, as this is a MFRC522 based clone.
